// Logisim project circuito_aula1.circ as structural Verilog: 1 circuit, main circuit main
module main (
  input  [31:0] Dado_a_ser_gravado,
  input  habilitaGrav,
  output [5:0] FUNCT,
  output [4:0] SHAMT,
  output [4:0] DESTINO,
  output [4:0] ORIGEM2,
  output [4:0] ORIGEM1,
  output [31:0] Saida_da_origem_1,
  output [5:0] OPCODE,
  output [31:0] Saida_da_origem_2
);

  wire CLK_out;

  // MIPSProgramROM mipsprogramrom_1: pin names not known; wires that end beside it: {32{1'b0}}, {OPCODE, ORIGEM1, ORIGEM2, DESTINO, SHAMT, FUNCT}
  Clock CLK (.out(CLK_out));
  // RegisterFile registerfile_1: pin names not known; wires that end beside it: Dado_a_ser_gravado, CLK_out, habilitaGrav, DESTINO, ORIGEM1, ORIGEM2, Saida_da_origem_1, Saida_da_origem_2

  // Notes on the sheet:
  //   Opcode | Origem1 | Origem2 | Destino | Shamt | Funct
endmodule
