// Logisim project circuito_aula2.circ as structural Verilog: 1 circuit, main circuit main
module main (
  input  REG_DEST,
  input  [3:0] ALU_OP,
  input  habilitaGrav,
  input  ALU_SOURCE
);

  wire CLK, registerfile_1_p1, registerfile_1_p7;
  wire [4:0] mipsprogramrom_1_p2_2, multiplexer_1_out;
  wire [31:0] adder_1_out, bit_extender_1_out, mipsprogramrom_1_p2, multiplexer_2_out, register_1_q,
       registerfile_1_p8;

  Register #(.width(32)) register_1 (.D(adder_1_out), .Q(register_1_q), .clk(CLK));  // open: en, clr
  Adder #(.width(32)) adder_1 (.a(register_1_q), .b(32'h4), .out(adder_1_out));  // open: cin, cout
  // MIPSProgramROM mipsprogramrom_1: pin names not known; wires that end beside it: register_1_q, {mipsprogramrom_1_p2[31:21], mipsprogramrom_1_p2_2, mipsprogramrom_1_p2[15:0]}
  Multiplexer #(.width(5)) multiplexer_1 (
    .in0(mipsprogramrom_1_p2[15:11]), .in1(mipsprogramrom_1_p2_2), .out(multiplexer_1_out), .sel(REG_DEST));  // open: en
  Clock clock_1 (.out(CLK));
  assign bit_extender_1_out = {{16{1'b0}}, mipsprogramrom_1_p2[15:0]};  // Bit_Extender bit_extender_1
  // RegisterFile registerfile_1: pin names not known; wires that end beside it: registerfile_1_p1, CLK, habilitaGrav, multiplexer_1_out, mipsprogramrom_1_p2[25:21], mipsprogramrom_1_p2_2, registerfile_1_p7, registerfile_1_p8
  Multiplexer #(.width(32)) multiplexer_2 (
    .in0(registerfile_1_p8), .in1(bit_extender_1_out), .out(multiplexer_2_out), .sel(ALU_SOURCE));  // open: en
  // Mips_ALU mips_alu_1: pin names not known; wires that end beside it: registerfile_1_p7, multiplexer_2_out, ALU_OP, registerfile_1_p1

  // Notes on the sheet:
  //   Tipo I
  //   Tipo R
  //   R
  //   I
  //   Primeira Origem
  //   Segunda Origem
  //   Destino
  //   Estender bits (Imediato)
  //   ADD - 001x com x - >náo importa
endmodule
